# Fritzing sketch smart walker (saved by Fritzing 0.9.3b)
breadboards: 1

parts:
  Part1 = Arduino Uno (Rev3)
  hc-sr1 = hc-sr04
  hc-sr2 = hc-sr04
  hc-sr3 = hc-sr04
  hc-sr4 = hc-sr04
  J1 = Piezo Speaker  # not connected

nets:
  N1: Part1.D2, hc-sr4.Trig, hc-sr4.Echo
  N2: Part1.D3_PWM, hc-sr3.Trig, hc-sr3.Echo
  N3: Part1.D4, hc-sr2.Trig, hc-sr2.Echo
  N4: Part1.D5_PWM, hc-sr1.Trig, hc-sr1.Echo
  VCC: Part1.5V, hc-sr1.VCC, hc-sr2.VCC, hc-sr3.VCC, hc-sr4.VCC
  GND: Part1.GND, hc-sr1.GND, hc-sr2.GND, hc-sr3.GND, hc-sr4.GND
